# Fritzing sketch Diagrama (saved by Fritzing 0.9.3b)

parts:
  Part1 = Arduino Uno (Rev3) - ICSP  # not connected
  Part2 = PWM Shield
  J1 = Basic Servo
  J2 = Basic Servo
  J3 = Basic Servo
  J4 = Basic Servo
  J5 = Basic Servo
  J6 = Basic Servo
  Part3 = Triple Axis Gyro Breakout ITG-3200
  U2 = POT [package=pot_mammoth]
  J7 = Power Jack [package=power_jack_pth_lock]
  U3 = Mini-360 DC-DC Buck converter [package=THT]
  U4 = POT [package=pot_mammoth]
  JP1 = USB_MICROB_PLUG [package=micro-b-ra-smt]  # not connected
  J8 = Piezo Speaker
  S1 = Round Pushbutton

nets:
  N1: Part2.OUT0, J1.vcc
  N2: Part2.OUT1, J2.vcc
  N3: Part2.OUT2, J3.vcc
  N4: Part2.OUT3, J5.vcc
  N5: Part2.OUT4, J4.vcc
  N6: Part2.OUT5, J6.vcc
  GND: Part2.GND, Part2.GND_-_GND@0, Part2.GND_-_GND@1, Part3.GND, U3.OUT-, J8.pin1
  N7: Part2.VIN, U3.OUT+
  N8: Part2.5V_A, Part3.VCC, S1.leg1
  N9: Part2.A0, U2.A
  N10: Part2.A1, U4.A
  N11: Part2.A4, Part3.SDA
  N12: Part2.A5, Part3.SCL
  N13: Part2.XLAT_-_D9, J8.pin2
  N14: U2.S, U4.S
  N15: J7.GNDBREAK, U3.IN+

custom parts:
  Mini-360 DC-DC Buck converter: Mini-360 DC-DC Buck converter. Tiny buck step down voltage converter, input voltage 4.75 to 23V output 1 to 17V adjustable. Available from ebay and the like.
